# Fritzing sketch removir_breadboard (saved by Fritzing 0.9.3b)
circuit board: 8.46667cm x 5.64444cm

parts:
  WeMos_D1_Mini1 = WeMos D1 Mini
  WS2812B1 = WS2812B 12V Strip -- White (60/m)
  CCS811 = CJMCU-811
  BMP_280 = Barometric Pressure Sensor - BMP180 Breakout (GY-68)
  M1 = Stepper Motor - Unipolar
  AC_220_V = Lilypad Battery Connect
  Velocidad = Pushbutton [package="[THT]"]
  Adaptador_12V_DC = Monacor line transformer [part_number=LTR-110]
  7805 = Voltage Regulator - 5V [package="DPak [SMD]"]
  470uf = Capacitor Polarized [package=cpol-radial-100uf-25v]
  470uf1 = Capacitor Polarized [package=cpol-radial-100uf-25v]
  KY-1 = Keyes Relay [package=THT]
  KY-2 = Keyes Relay [package=THT]
  KY-3 = Keyes Relay [package=THT]
  KY-4 = Keyes Relay [package=THT]

nets:
  3V3: WeMos_D1_Mini1.3V3, CCS811.VCC
  N1: WeMos_D1_Mini1.5V, WS2812B1.DI, 7805.input_voltage, 470uf.+, KY-1.power, KY-2.power, KY-3.power, KY-4.power
  N2: WeMos_D1_Mini1.D1, CCS811.SCL, BMP_280.SCL
  N3: WeMos_D1_Mini1.D2, CCS811.SDA, BMP_280.SDA
  N4: WeMos_D1_Mini1.D3, WS2812B1.+12V
  N5: WeMos_D1_Mini1.D4, Velocidad.Pin_2
  N6: WeMos_D1_Mini1.D5, KY-1.signal
  N7: WeMos_D1_Mini1.D6, KY-2.signal
  N8: WeMos_D1_Mini1.D7, KY-3.signal
  N9: WeMos_D1_Mini1.D8, KY-4.signal
  GND: WeMos_D1_Mini1.G, WS2812B1.GND, CCS811.GND, CCS811.WAK, BMP_280.GND, AC_220_V.-, Velocidad.Pin_3, Velocidad.Pin_4, Adaptador_12V_DC.GND, 7805.GND, 470uf.-, 470uf1.-, KY-1.ground, KY-1.C, KY-2.ground, KY-2.C, KY-3.ground, KY-3.C, KY-4.ground, KY-4.C
  N10: M1.A, KY-4.NO
  N11: M1.COMMON_1, KY-3.NO
  N12: M1.C, M1.D, AC_220_V.+, Adaptador_12V_DC.01
  N13: M1.B, KY-2.NO
  N14: M1.COMMON_2, KY-1.NO
  N15: Adaptador_12V_DC.02, 7805.output_voltage, 470uf1.+

custom parts:
  WS2812B 12V Strip -- White (60/m): WS2812B LED Strip, White, 60 pixels per meter, 12V Power
  CJMCU-811: The CCS811 is an ultra-low power digital gas sensor solution which integrates a metal oxide (MOX) gas sensor to detect a wide range of Volatile Organic Compounds (VOCs) for indoor air quality monitoring with a microcontroller unit (MCU), which includes an Analog-to-Digital converter (ADC), and an I²C interface.
  Keyes Relay: The Keyes 5V relay module is suitable for SCM development, home appliance control. It uses a 5V~12V TIL control signal which can control DC / AC signal.
